// Logisim project Calc.circ as structural Verilog: 3 circuits, main circuit main
module main (
  input  in_1,
  input  in_2,
  input  in_3,
  input  in_4,
  input  in_5,
  input  in_6,
  input  in_7,
  input  in_8,
  input  in_9,
  input  in_10,
  input  in_11,
  input  in_12,
  input  in_13,
  input  in_14,
  input  in_15,
  input  in_16
);

  wire retenue_1_retenue, retenue_2_retenue, retenue_3_retenue, retenue_4_retenue, tabresult_1_a_2,
       tabresult_1_b_2, tabresult_1_c_2, tabresult_1_d_2, tabresult_1_e, tabresult_1_f, tabresult_1_g,
       tabresult_2_a_2, tabresult_2_b_2, tabresult_2_c_2, tabresult_2_d_2, tabresult_2_e, tabresult_2_f,
       tabresult_2_g, tabresult_3_a_2, tabresult_3_b_2, tabresult_3_c_2, tabresult_3_d_2, tabresult_3_e,
       tabresult_3_f, tabresult_3_g, tabresult_4_a_2, tabresult_4_b_2, tabresult_4_c_2, tabresult_4_d_2,
       tabresult_4_e, tabresult_4_f, tabresult_4_g;

  tabResult tabresult_1 (
    .D(in_1), .C(in_2), .B(in_3), .A(in_4), .a_2(tabresult_1_a_2), .b_2(tabresult_1_b_2),
    .c_2(tabresult_1_c_2), .d_2(tabresult_1_d_2), .e(tabresult_1_e), .f(tabresult_1_f), .g(tabresult_1_g));
  LED led_1 (.in(retenue_1_retenue));
  Retenue retenue_1 (.D(in_1), .C(in_2), .B(in_3), .A(in_4), .retenue(retenue_1_retenue));
  tabResult tabresult_2 (
    .D(in_5), .C(in_6), .B(in_7), .A(in_8), .a_2(tabresult_2_a_2), .b_2(tabresult_2_b_2),
    .c_2(tabresult_2_c_2), .d_2(tabresult_2_d_2), .e(tabresult_2_e), .f(tabresult_2_f), .g(tabresult_2_g));
  LED led_2 (.in(retenue_2_retenue));
  Retenue retenue_2 (.D(in_5), .C(in_6), .B(in_7), .A(in_8), .retenue(retenue_2_retenue));
  tabResult tabresult_3 (
    .D(in_9), .C(in_10), .B(in_11), .A(in_12), .a_2(tabresult_3_a_2), .b_2(tabresult_3_b_2),
    .c_2(tabresult_3_c_2), .d_2(tabresult_3_d_2), .e(tabresult_3_e), .f(tabresult_3_f), .g(tabresult_3_g));
  LED led_3 (.in(retenue_3_retenue));
  Retenue retenue_3 (.D(in_9), .C(in_10), .B(in_11), .A(in_12), .retenue(retenue_3_retenue));
  tabResult tabresult_4 (
    .D(in_13), .C(in_14), .B(in_15), .A(in_16), .a_2(tabresult_4_a_2), .b_2(tabresult_4_b_2),
    .c_2(tabresult_4_c_2), .d_2(tabresult_4_d_2), .e(tabresult_4_e), .f(tabresult_4_f), .g(tabresult_4_g));
  LED led_4 (.in(retenue_4_retenue));
  Retenue retenue_4 (.D(in_13), .C(in_14), .B(in_15), .A(in_16), .retenue(retenue_4_retenue));
  _7_Segment_Display u_7_segment_display_1 (
    .g(tabresult_1_g), .f(tabresult_1_f), .a(tabresult_1_a_2), .b(tabresult_1_b_2), .e(tabresult_1_e),
    .d(tabresult_1_d_2), .c(tabresult_1_c_2));  // open: dp
  _7_Segment_Display u_7_segment_display_2 (
    .g(tabresult_2_g), .f(tabresult_2_f), .a(tabresult_2_a_2), .b(tabresult_2_b_2), .e(tabresult_2_e),
    .d(tabresult_2_d_2), .c(tabresult_2_c_2));  // open: dp
  _7_Segment_Display u_7_segment_display_3 (
    .g(tabresult_3_g), .f(tabresult_3_f), .a(tabresult_3_a_2), .b(tabresult_3_b_2), .e(tabresult_3_e),
    .d(tabresult_3_d_2), .c(tabresult_3_c_2));  // open: dp
  _7_Segment_Display u_7_segment_display_4 (
    .g(tabresult_4_g), .f(tabresult_4_f), .a(tabresult_4_a_2), .b(tabresult_4_b_2), .e(tabresult_4_e),
    .d(tabresult_4_d_2), .c(tabresult_4_c_2));  // open: dp

  // Notes on the sheet:
  //   tabResult
  //   Retenue
  //   tabResult
  //   Retenue
  //   tabResult
  //   Retenue
  //   tabResult
  //   Retenue
endmodule

module tabResult (
  input  D,
  input  C,
  input  B,
  input  A,
  output a_2,
  output b_2,
  output c_2,
  output d_2,
  output e,
  output f,
  output g
);

  wire and_1_out, and_2_out, and_3_out, and_4_out, and_5_out, and_6_out, and_7_out, and_8_out, and_9_out,
       and_10_out, and_11_out, and_12_out, and_13_out, and_14_out, and_15_out, and_16_out, and_17_out,
       and_18_out, and_19_out, not_1_out, not_2_out, not_3_out, not_4_out, not_5_out, not_6_out, not_7_out,
       not_8_out, not_9_out, not_10_out, not_11_out, not_12_out, not_13_out, not_14_out, not_15_out,
       not_16_out, not_17_out, not_18_out, not_19_out, not_20_out, not_21_out, not_22_out, not_23_out,
       or_1_out, or_2_out, or_3_out, or_4_out, or_5_out, or_6_out, or_8_out, or_9_out, or_10_out, or_11_out,
       or_12_out, or_15_out, or_16_out;

  not not_1 (not_1_out, C);
  and and_1 (and_1_out, not_1_out, not_2_out);
  not not_2 (not_2_out, A);
  and and_2 (and_2_out, C, A);
  not not_3 (not_3_out, C);
  not not_4 (not_4_out, B);
  and and_3 (and_3_out, not_4_out, not_5_out);
  not not_5 (not_5_out, A);
  and and_4 (and_4_out, B, A);
  not not_6 (not_6_out, B);
  or or_1 (or_1_out, not_6_out, A);
  or or_2 (or_2_out, C, D);
  not not_7 (not_7_out, C);
  and and_5 (and_5_out, not_7_out, not_8_out);
  not not_8 (not_8_out, A);
  not not_9 (not_9_out, C);
  and and_6 (and_6_out, not_9_out, B);
  not not_10 (not_10_out, A);
  and and_7 (and_7_out, C, not_11_out);
  not not_11 (not_11_out, B);
  not not_12 (not_12_out, C);
  and and_8 (and_8_out, not_12_out, not_13_out);
  not not_13 (not_13_out, B);
  not not_14 (not_14_out, A);
  not not_15 (not_15_out, D);
  and and_9 (and_9_out, not_15_out, B);
  not not_16 (not_16_out, A);
  not not_17 (not_17_out, B);
  and and_10 (and_10_out, not_17_out, not_18_out);
  not not_18 (not_18_out, A);
  and and_11 (and_11_out, C, not_19_out);
  not not_19 (not_19_out, B);
  and and_12 (and_12_out, C, not_20_out);
  not not_20 (not_20_out, A);
  not not_21 (not_21_out, C);
  and and_13 (and_13_out, not_21_out, B);
  and and_14 (and_14_out, C, not_22_out);
  not not_22 (not_22_out, B);
  and and_15 (and_15_out, C, not_23_out);
  not not_23 (not_23_out, A);
  or or_3 (or_3_out, and_1_out, B);
  or or_4 (or_4_out, and_2_out, D);
  or or_5 (or_5_out, not_3_out, and_3_out);
  or or_6 (or_6_out, and_4_out, D);
  or or_7 (c_2, or_1_out, or_2_out);
  or or_8 (or_8_out, and_5_out, and_6_out);
  and and_16 (and_16_out, B, not_10_out);
  and and_17 (and_17_out, and_7_out, A);
  and and_18 (and_18_out, and_8_out, not_14_out);
  and and_19 (and_19_out, and_9_out, not_16_out);
  or or_9 (or_9_out, and_10_out, and_11_out);
  or or_10 (or_10_out, and_12_out, D);
  or or_11 (or_11_out, and_13_out, and_14_out);
  or or_12 (or_12_out, and_15_out, D);
  or or_13 (a_2, or_3_out, or_4_out);
  or or_14 (b_2, or_5_out, or_6_out);
  or or_15 (or_15_out, or_8_out, and_16_out);
  or or_16 (or_16_out, and_17_out, D);
  or or_17 (e, and_18_out, and_19_out);
  or or_18 (f, or_9_out, or_10_out);
  or or_19 (g, or_11_out, or_12_out);
  or or_20 (d_2, or_15_out, or_16_out);
endmodule

module Retenue (
  input  D,
  input  C,
  input  B,
  input  A,
  output retenue
);

  wire and_1_out, and_2_out;

  and and_1 (and_1_out, D, B);
  and and_2 (and_2_out, D, C);
  or or_1 (retenue, and_1_out, and_2_out);
endmodule
